# Fritzing sketch LineCar (saved by Fritzing 0.9.2b)
breadboards: 1

parts:
  L-Sensor = PHOTOTRANSISTOR REFLECTIVE OBJECT SENSOR [package=qrb1114-side]
  R-Sensor = PHOTOTRANSISTOR REFLECTIVE OBJECT SENSOR [package=qrb1114-side]
  part = Resistor [tolerance=±5% resistance=10k package=THT]
  part_2 = Resistor [tolerance=±5% resistance=200 package=THT]
  R4 = Resistor [tolerance=±5% resistance=10k package=THT]
  part_3 = Resistor [tolerance=±5% resistance=200 package=THT]
  Adafruit_Motorshield = Arduino Motor Shield (Rev3)
  L-Motor = DC Motor
  R-Motor = DC Motor

nets:
  N1: L-Sensor.A, part_2.Pin_1
  N2: L-Sensor.C, R4.Pin_1, Adafruit_Motorshield.A1
  N3: L-Sensor.E, L-Sensor.K, R-Sensor.E, R-Sensor.K, Adafruit_Motorshield.GND
  N4: R-Sensor.A, part_3.Pin_1
  N5: R-Sensor.C, part.Pin_1, Adafruit_Motorshield.A0
  N6: part.Pin_0, part_2.Pin_0, R4.Pin_0, part_3.Pin_0, Adafruit_Motorshield.5V
  N7: Adafruit_Motorshield.B-, L-Motor.pin_2
  N8: Adafruit_Motorshield.B+, L-Motor.pin_1
  N9: Adafruit_Motorshield.A-, R-Motor.pin_2
  N10: Adafruit_Motorshield.A+, R-Motor.pin_1
